// Logisim project S1-T10.circ as structural Verilog: 7 circuits, main circuit main
module main (
  input  [7:0] Temperature,
  input  Reset,
  input  Control_Input,
  input  in_4,
  input  in_5,
  output [4:0] BPM,
  output [4:0] out_7
);

  wire BPM_Monitor_state, Control_System_bpm_2, Control_System_temp_2, Fall_Detection_fall_state, Fall_out,
       Medicine_Reminder_medicine_reminder, Mono_Pulse_out, not_1_out, not_2_out, or_1_out, or_2_out,
       Reset_out, Temperature_Monitor_out_2;
  wire [7:0] and_1_out_10;

  Button Mono_Pulse (.out(Mono_Pulse_out));
  Button Fall (.out(Fall_out));
  Button u_Reset (.out(Reset_out));
  Control_system Control_System (
    .BPM(Control_Input), .Temp(in_4), .Idle(in_5), .BPM_2(Control_System_bpm_2),
    .Temp_2(Control_System_temp_2));  // open: Idle_2
  Fall_Detection Fall_Detection (.Fall_Detector(Fall_out), .Reset(Reset_out), .Fall_State(Fall_Detection_fall_state));
  not not_1 (not_1_out, Reset);
  not not_2 (not_2_out, Control_System_bpm_2);
  BPM_Monitor BPM_Monitor (
    .MonoPulse(Mono_Pulse_out), .Reset(or_1_out), .Carry(BPM), .BPM(out_7), .State(BPM_Monitor_state));
  or or_1 (or_1_out, not_1_out, not_2_out);
  \and  and_1 (
    .enable(Control_System_temp_2), .IO(Temperature[0]), .in_3(Temperature[1]), .in_4(Temperature[2]),
    .in_5(Temperature[3]), .in_6(Temperature[4]), .in_7(Temperature[5]), .in_8(Temperature[6]),
    .in_9(Temperature[7]), .out_10(and_1_out_10));
  Temperature_Monitor Temperature_Monitor (.Temp(and_1_out_10), .out_2(Temperature_Monitor_out_2));
  Medicine_Reminder Medicine_Reminder (.Medicine_Reminder(Medicine_Reminder_medicine_reminder));
  or or_2 (or_2_out, Medicine_Reminder_medicine_reminder, Temperature_Monitor_out_2, BPM_Monitor_state, Fall_Detection_fall_state);
  LED led_1 (.in(or_2_out));

  // Notes on the sheet:
  //   3. Put 001in the control system for Idle State
  //   2. Put 010 in the control system, enter the temperature of the patient manually, this will give you the output
  //   Instructions
  //   1. Put 100 in the control system, and then toggle the reset buttoon to 0. In the next 10 seconds, give the mono pulse beat, which will give ou the output.
  //   4. If the fall signal passes the debouncing system, then a recovery timer starts. Press the reset button before 30 seconds, or else the alarm goes off.
  //   Team S1-T10
  //   1. Aayushman 231CS115
  //   2. Atharva Parkhi 231CS115
  //   3. Sahil Mengji 231CS151
endmodule

module \and  (
  input  enable,
  input  IO,
  input  in_3,
  input  in_4,
  input  in_5,
  input  in_6,
  input  in_7,
  input  in_8,
  input  in_9,
  output [7:0] out_10
);

  and and_1 (out_10[0], IO, enable);
  and and_2 (out_10[1], in_3, enable);
  and and_3 (out_10[2], in_4, enable, enable);
  and and_4 (out_10[3], in_5, enable);
  and and_5 (out_10[4], in_6, enable);
  and and_6 (out_10[5], in_7, enable);
  and and_7 (out_10[6], in_8, enable);
  and and_8 (out_10[7], in_9, enable);
endmodule

module BPM_Monitor (
  input  MonoPulse,
  input  Reset,
  output [4:0] Carry,
  output [4:0] BPM,
  output State
);

  wire and_1_out, and_2_out, clock_1_out, comparator_1_eq, comparator_2_eq, comparator_2_gt, comparator_2_lt,
       comparator_3_eq, comparator_3_gt, comparator_3_lt, nand_1_out, not_1_out, or_1_out, or_2_out, or_3_out;
  wire [3:0] counter_1_q;
  wire [4:0] counter_2_q;

  Clock #(.highDuration(400), .lowDuration(400)) clock_1 (.out(clock_1_out));
  and and_1 (and_1_out, clock_1_out, not_1_out);
  Counter #(.width(4), .max('ha)) counter_1 (
    .Q(counter_1_q), .clk(and_1_out), .clr(Reset));  // open: load, D, count, carry
  not not_1 (not_1_out, comparator_1_eq);
  and and_2 (and_2_out, MonoPulse, not_1_out);
  Comparator #(.width(4)) comparator_1 (.a(counter_1_q), .b(4'b1010), .eq(comparator_1_eq));  // open: gt, lt
  Counter #(.width(5), .max('h1f)) counter_2 (
    .Q(counter_2_q), .clk(and_2_out), .clr(Reset));  // open: load, D, count, carry
  Comparator #(.width(5), .mode("unsigned")) comparator_2 (
    .a(counter_2_q), .b(5'b01010), .gt(comparator_2_gt), .eq(comparator_2_eq), .lt(comparator_2_lt));
  Comparator #(.width(5), .mode("unsigned")) comparator_3 (
    .a(counter_2_q), .b(5'b10001), .gt(comparator_3_gt), .eq(comparator_3_eq), .lt(comparator_3_lt));
  Multiplier #(.width(5)) multiplier_1 (.a(5'b00110), .b(counter_2_q), .out(BPM), .cout(Carry));  // open: cin
  or or_1 (or_1_out, comparator_2_eq, comparator_2_gt);
  or or_2 (or_2_out, comparator_3_gt, comparator_3_eq);
  nand nand_1 (nand_1_out, or_1_out, comparator_3_lt);
  or or_3 (or_3_out, comparator_2_lt, or_2_out, nand_1_out);
  and and_3 (State, comparator_1_eq, or_3_out);

  // Notes on the sheet:
  //   BPM Monitor
endmodule

module Temperature_Monitor (
  input  [7:0] Temp,
  output out_2
);

  wire and_1_out, comparator_1_eq, comparator_1_gt, comparator_1_lt, comparator_2_eq, comparator_2_gt,
       comparator_2_lt, nand_1_out, nor_1_out, nor_2_out, not_1_out, or_1_out, or_2_out, or_3_out;

  nor nor_1 (nor_1_out, Temp[0], Temp[1], Temp[2], Temp[3], Temp[4]);
  nor nor_2 (nor_2_out, Temp[5], Temp[6], Temp[7]);
  Comparator #(.mode("unsigned")) comparator_1 (
    .a(Temp), .b(8'h61), .gt(comparator_1_gt), .eq(comparator_1_eq), .lt(comparator_1_lt));
  Comparator #(.mode("unsigned")) comparator_2 (
    .a(Temp), .b(8'h64), .gt(comparator_2_gt), .eq(comparator_2_eq), .lt(comparator_2_lt));
  and and_1 (and_1_out, nor_1_out, nor_2_out, nor_2_out);
  or or_1 (or_1_out, comparator_1_eq, comparator_1_gt);
  not not_1 (not_1_out, and_1_out);
  or or_2 (or_2_out, comparator_2_gt, comparator_2_eq);
  nand nand_1 (nand_1_out, or_1_out, comparator_2_lt);
  or or_3 (or_3_out, comparator_1_lt, or_2_out, nand_1_out);
  and and_2 (out_2, not_1_out, or_3_out);

  // Notes on the sheet:
  //   Temperature Monitor
endmodule

module Medicine_Reminder (
  output Medicine_Reminder
);

  wire and_1_out, and_2_out, clock_1_out, clock_3_out, comparator_2_eq, not_1_out;
  wire [7:0] Timer_q;
  wire [11:0] Clock_2_q;

  Clock #(.highDuration(400), .lowDuration(400)) clock_1 (.out(clock_1_out));
  and and_1 (and_1_out, clock_1_out, not_1_out);
  Counter #(.width(12), .max('hfff)) Clock_2 (
    .Q(Clock_2_q), .clk(and_1_out), .clr(comparator_2_eq));  // open: load, D, count, carry
  Comparator #(.width(12), .mode("unsigned")) comparator_1 (
    .a(12'h258), .b(Clock_2_q), .eq(Medicine_Reminder));  // open: gt, lt
  not not_1 (not_1_out, Medicine_Reminder);
  Clock #(.highDuration(400), .lowDuration(400)) clock_3 (.out(clock_3_out));
  Counter #(.max('ha)) Timer (.Q(Timer_q), .clk(and_2_out), .clr(comparator_2_eq));  // open: load, D, count, carry
  and and_2 (and_2_out, clock_3_out, Medicine_Reminder);
  Comparator #(.mode("unsigned")) comparator_2 (.a(8'ha), .b(Timer_q), .eq(comparator_2_eq));  // open: gt, lt

  // Notes on the sheet:
  //   Medicine Reminder
endmodule

module Fall_Detection (
  input  Fall_Detector,
  input  Reset,
  output Fall_State
);

  wire and_1_out, and_2_out, and_3_out, clock_1_out, clock_2_out, clock_3_out, d_ff_1_q, d_ff_2_q, s_r_ff_1_q;
  wire [4:0] counter_1_q;

  Clock clock_1 (.out(clock_1_out));
  D_Flip_Flop d_ff_1 (.clk(clock_1_out), .D(Fall_Detector), .Q(d_ff_1_q));  // open: Qn, preset, en, reset
  D_Flip_Flop d_ff_2 (.clk(clock_1_out), .D(d_ff_1_q), .Q(d_ff_2_q));  // open: Qn, preset, en, reset
  Clock #(.highDuration(1001), .lowDuration(1001)) clock_2 (.out(clock_2_out));
  Clock #(.highDuration(400), .lowDuration(400)) clock_3 (.out(clock_3_out));
  and and_1 (and_1_out, clock_3_out, clock_3_out, s_r_ff_1_q, s_r_ff_1_q);
  and and_2 (and_2_out, d_ff_2_q, d_ff_1_q);
  Counter #(.width(5), .max('h1f)) counter_1 (
    .Q(counter_1_q), .clk(and_1_out), .clr(Reset));  // open: load, D, count, carry
  S_R_Flip_Flop s_r_ff_1 (
    .S(and_2_out), .clk(clock_2_out), .R(Reset), .Q(s_r_ff_1_q), .reset(Reset));  // open: Qn, preset, en
  and and_3 (and_3_out, counter_1_q[1], counter_1_q[2], counter_1_q[3], counter_1_q[4]);
  S_R_Flip_Flop s_r_ff_2 (
    .S(and_3_out), .clk(clock_2_out), .R(Reset), .Q(Fall_State), .reset(Reset));  // open: Qn, preset, en

  // Notes on the sheet:
  //   Fall Detection
endmodule

module Control_system (
  input  BPM,
  input  Temp,
  input  Idle,
  output BPM_2,
  output Temp_2,
  output Idle_2
);

  wire and_1_out, clock_1_out, d_ff_1_q, d_ff_1_qn, d_ff_2_q, d_ff_2_qn, not_1_out, not_2_out;

  Clock #(.highDuration(400), .lowDuration(400)) clock_1 (.out(clock_1_out));
  and and_1 (and_1_out, BPM, not_1_out);
  not not_1 (not_1_out, Idle);
  D_Flip_Flop d_ff_1 (.clk(clock_1_out), .D(and_1_out), .Q(d_ff_1_q), .Qn(d_ff_1_qn));  // open: preset, en, reset
  D_Flip_Flop d_ff_2 (.clk(clock_1_out), .D(Temp), .Q(d_ff_2_q), .Qn(d_ff_2_qn));  // open: preset, en, reset
  and and_2 (BPM_2, d_ff_1_q, not_2_out);
  not not_2 (not_2_out, d_ff_2_q);
  and and_3 (Temp_2, d_ff_1_qn, d_ff_2_q);
  and and_4 (Idle_2, d_ff_1_qn, d_ff_2_qn);

  // Notes on the sheet:
  //   Control System
endmodule
